// Logisim project cpu_risc_v.circ as structural Verilog
module main (
);

  Register #(.width(32)) register_1 ();  // open: D, en, clk, Q, clr
endmodule

module fp_register_file (
);

  Register #(.width(32)) register_1 ();  // open: D, en, clk, Q, clr
  Register #(.width(32)) register_2 ();  // open: D, en, clk, Q, clr
  Register #(.width(32)) register_3 ();  // open: D, en, clk, Q, clr
  Register #(.width(32)) register_4 ();  // open: D, en, clk, Q, clr
  Register #(.width(32)) register_5 ();  // open: D, en, clk, Q, clr
  Register #(.width(32)) register_6 ();  // open: D, en, clk, Q, clr
  Register #(.width(32)) register_7 ();  // open: D, en, clk, Q, clr
  Register #(.width(32)) register_8 ();  // open: D, en, clk, Q, clr
  Register #(.width(32)) register_9 ();  // open: D, en, clk, Q, clr
  Register #(.width(32)) register_10 ();  // open: D, en, clk, Q, clr
  Register #(.width(32)) register_11 ();  // open: D, en, clk, Q, clr
  Register #(.width(32)) register_12 ();  // open: D, en, clk, Q, clr
endmodule

module vector_register (
  input  WriteEnable,
  input  [31:0] Input_0,
  input  Clock,
  input  [31:0] Input_1,
  input  [31:0] Input_2,
  input  ReadEnable,
  output [31:0] Output_0,
  output [31:0] Output_1,
  output [31:0] Output_2
);

  Register #(.width(32)) v_sub_0 (.D(Input_0), .en(WriteEnable), .clk(Clock), .Q(Output_0), .clr(ReadEnable));
  Register #(.width(32)) v_sub_1 (.D(Input_1), .en(WriteEnable), .clk(Clock), .Q(Output_1), .clr(ReadEnable));
  Register #(.width(32)) v_sub_2 (.D(Input_2), .en(WriteEnable), .clk(Clock), .Q(Output_2), .clr(ReadEnable));
endmodule
